# Fritzing sketch Arduino bme280 oled (saved by Fritzing 0.9.2b)

parts:
  OLED1 = 128x32 I2C Monochrome OLED Display
  Part1 = BME280 Breakout
  Part2 = Arduino Uno (Rev3)

nets:
  N1: OLED1.SDA, Part2.A4/SDA
  N2: OLED1.SCL, Part2.A5/SCL
  GND: OLED1.GND, Part1.GND, Part2.GND
  3.3V: OLED1.3.3V, Part1.3.3V, Part2.3V3
  N3: Part1.!CS, Part2.D10_PWM/SS
  N4: Part1.SDI/SDA, Part2.D11_PWM/MOSI
  N5: Part1.SDO/ADR, Part2.D12/MISO
  N6: Part1.SCK/SCL, Part2.D13/SCK
