# Fritzing sketch arduino and ADXL335 (saved by Fritzing 0.9.3b)

parts:
  Part1 = Adafruit ADXL335 [part_number="Adafruit #163"]
  Part2 = Arduino Uno (Rev3)

nets:
  +3V3: Part1.+3V3, Part2.3V3
  GND: Part1.GND, Part2.GND
  N1: Part1.ZOUT, Part2.A2
  N2: Part1.YOUT, Part2.A1
  N3: Part1.XOUT, Part2.A0

custom parts:
  Adafruit ADXL335: We've updated our favorite triple-axis accelerometer to now have an on-board 3.3V regulator - making it a perfect choice for interfacing with a 5V microcontroller such as the Arduino. This breakout comes with 3 analog outputs for X, Y and Z axis measurements on a 0.75"x0.75" breakout board. The ADXL335 is the latest and greatest from Analog Devices, known for their exceptional quality MEMS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
