# Fritzing sketch arduino and APDS9930 (saved by Fritzing 0.9.3b)

parts:
  PART1 = APDS-9960 RGB and Gesture Sensor [part_number=SEN-12787]
  Part1 = Arduino Uno (Rev3)

nets:
  VCC: PART1.VCC, Part1.3V3
  GND: PART1.GND, Part1.GND
  N1: PART1.SDA, Part1.A4/SDA
  N2: PART1.SCL, Part1.A5/SCL

custom parts:
  APDS-9960 RGB and Gesture Sensor: Breakout board for the Avago APDS-9960 proximity, light, RGB, and gesture sensors. Please visit www.sparkfun.com to learn more.
