# Fritzing sketch arduino and GA1A1S202WP (saved by Fritzing 0.9.3b)

parts:
  Part6 = Arduino Uno (Rev3)
  Part10 = Adafruit GA1A1S202WP [part_number="Adafruit #1384"]

nets:
  N1: Part6.A0, Part10.OUT
  5V: Part6.5V, Part10.VCC
  GND: Part6.GND, Part10.GND

custom parts:
  Adafruit GA1A1S202WP: Upgrade a project that uses a photocell with the GA1A12S202 analog light sensor. Like a CdS photo-cell, the sensor does not require a microcontroller, the analog voltage output increases with the amount of light shining on the sensor face. This sensor has a lot of improvements that make it better for nearly any project. The biggest improvement over plain photocells is a true log-lin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
