# Fritzing sketch arduino and GUVAS12SD (saved by Fritzing 0.9.3b)

parts:
  Part2 = Arduino Uno (Rev3)
  Part3 = GUVA-S12SD UV Light Sensor

nets:
  N1: Part2.A0, Part3.Out
  5V: Part2.5V, Part3.5V
  GND: Part2.GND, Part3.GND

custom parts:
  GUVA-S12SD UV Light Sensor: Extend your light-sensing spectrum with this analog UV sensor module. It uses a UV photodiode, which can detect the 240-370nm range of light (which covers UVB and most of UVA spectrum). The signal level from the photodiode is very small, in the nano-ampere level, so we tossed on an opamp to amplify the signal to a more manageable volt-level.
