# Fritzing sketch arduino and MMA8451 (saved by Fritzing 0.9.3b)

parts:
  Part6 = Arduino Uno (Rev3)
  Part9 = Adafruit MMA8451 Accelerometer [part_number="Adafruit #2019"]

nets:
  N1: Part6.A4/SDA, Part9.SDA
  N2: Part6.A5/SCL, Part9.SCL
  5V: Part6.5V, Part9.VIN
  GND: Part6.GND, Part9.GND

custom parts:
  Adafruit MMA8451 Accelerometer: So many accelerometers and so little time! We've expanded our accelerometer selection even more with this high-precision and inexpensive MMA8451 Triple-Axis Accelerometer w/ 14-bit ADC. You can detect motion, tilt and basic orientation with a digital accelerometer - and the MMA8451 is a great accelerometer to start with. It has a wide usage range, from +-2g up to +-8g yet is easy to use with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
