# Fritzing sketch arduino and TSL2561 (saved by Fritzing 0.9.3b)

parts:
  Part6 = Arduino Uno (Rev3)
  Part11 = Adafruit TSL2561 [part_number="Adafruit #439"]

nets:
  N1: Part6.A4/SDA, Part11.SDA
  N2: Part6.A5/SCL, Part11.SCL
  5V: Part6.5V, Part11.VIN
  GND: Part6.GND, Part11.GND

custom parts:
  Adafruit TSL2561: The TSL2561 luminosity sensor is an advanced digital light sensor, ideal for use in a wide range of light situations. Compared to low cost CdS cells, this sensor is more precise, allowing for exact lux calculations and can be configured for different gain/timing ranges to detect light ranges from up to 0.1 - 40,000+ Lux on the fly. The best part of this sensor is that it contains both infrared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
