# Fritzing sketch arduino and ads1015 (saved by Fritzing 0.9.2b)

parts:
  IC1 = ADS1015 12-bit ADC Breakout
  Part1 = Arduino Uno (Rev3)

nets:
  VDD: IC1.VDD, Part1.5V
  GND: IC1.GND, Part1.GND
  N1: IC1.SCL, Part1.A5/SCL
  N2: IC1.SDA, Part1.A4/SDA

custom parts:
  ADS1015 12-bit ADC Breakout: ADS1015 12-bit I2C ADC+PGA Breakout
