# Fritzing sketch arduino and attiny85 (saved by Fritzing 0.9.3b)
breadboards: 1

parts:
  U1 = ATTINY45 [package=dip]
  Part1 = Arduino Uno (Rev3)
  LED1 = LED - 5mm [color="Red (633nm)" package="5 mm [THT]"]
  R1 = Resistor [tolerance=±5% resistance=470 package=THT]
  C1 = Electrolytic Capacitor [capacitance=10µF voltage=16V package="100 mil [THT, electrolytic]"]

nets:
  N1: U1.PB5(NRES), Part1.D10_PWM/SS
  N2: U1.PB4(ADC2), R1.Pin_0
  GND: U1.GND, Part1.GND, LED1.cathode, C1.+
  N3: U1.PB0(MOSI), Part1.D11_PWM/MOSI
  N4: U1.PB1(MISO), Part1.D12/MISO
  N5: U1.PB2(SCK_ADC1), Part1.D13/SCK
  VCC: U1.VCC, Part1.5V
  N6: Part1.RESET, C1.-
  N7: LED1.anode, R1.Pin_1
