# Fritzing sketch arduino and bh1750 (saved by Fritzing 0.9.3b)

parts:
  Part1 = BH1750
  Part2 = Arduino Uno (Rev3)

nets:
  VCC: Part1.VCC, Part2.5V
  GND: Part1.GND, Part2.GND
  N1: Part1.SCL, Part2.A5/SCL
  N2: Part1.SDA, Part2.A4/SDA

custom parts:
  BH1750: Light Sensor
