# Fritzing sketch arduino and hdc1008 (saved by Fritzing 0.9.3b)

parts:
  Part1 = Arduino Uno (Rev3)
  Part2 = Adafruit HDC1008 Temperature Humidity Sensor [part_number="Adafruit #2635"]

nets:
  N1: Part1.A4/SDA, Part2.SDA
  N2: Part1.A5/SCL, Part2.SCL
  5V: Part1.5V, Part2.VDD
  GND: Part1.GND, Part2.GND

custom parts:
  Adafruit HDC1008 Temperature Humidity Sensor: This I2C digital humidity sensor is a fairly accurate and intelligent alternative to the much simpler Humidity and Temperature Sensor - SHT15 Breakout It has a typical accuracy of ±4% with an operating range that's optimized from 10% to 80% RH. Operation outside this range is still possible - just the accuracy might drop a bit. The temperature output has a typical accuracy of ±0.2°C from -20~85°C.
