# Fritzing sketch arduino and ir proximity (saved by Fritzing 0.9.3b)

parts:
  J1 = Infrared Proximity Sensor
  Part1 = Arduino Uno (Rev3)

nets:
  N1: J1.Vout, Part1.A0
  GND: J1.GND, Part1.GND
  VCC: J1.Vcc, Part1.5V
