# Fritzing sketch arduino and keypad (saved by Fritzing 0.9.3b)

parts:
  KEYPAD1 = Membrane Matrix Keypad
  Part1 = Arduino Uno (Rev3)

nets:
  N1: KEYPAD1.1, Part1.D9_PWM
  N2: KEYPAD1.2, Part1.D8
  N3: KEYPAD1.3, Part1.D7
  N4: KEYPAD1.4, Part1.D6_PWM
  N5: KEYPAD1.5, Part1.D5_PWM
  N6: KEYPAD1.6, Part1.D4
  N7: KEYPAD1.7, Part1.D3_PWM

notes:
  Pin 1
  Pin 1 = Row 1
  Pin 2 = Row 2
  Pin 3 = Row 3
  Pin 4 = Row 4
  Pin 5 = Column 1
  Pin 6 = Column 2
  Pin 7 = Column 3

custom parts:
  Membrane Matrix Keypad: Membrane Matrix 3x4 Keypad
