# Fritzing sketch arduino and mma7361 (saved by Fritzing 0.9.3b)

parts:
  Part2 = Arduino Uno (Rev3)
  U2 = MMA7361 [package=lga14]

nets:
  N1: Part2.A3, U2.ZOUT
  N2: Part2.A4/SDA, U2.YOUT
  N3: Part2.A5/SCL, U2.XOUT
  5V: Part2.5V, U2.VSS
  N4: Part2.GND, U2.G

custom parts:
  MMA7361: 3-axis 1.5/6g analog output accelerometer
