# Fritzing sketch arduino and mpu9250 (saved by Fritzing 0.9.3b)

parts:
  GY1 = GY-5150 (MPU-9150) [form="♀ (female)" package=THT]
  Part1 = Arduino Uno (Rev3)

nets:
  N1: GY1.pin1, Part1.3V3
  N2: GY1.pin2, Part1.GND
  N3: GY1.pin3, Part1.A5/SCL
  N4: GY1.pin4, Part1.A4/SDA

custom parts:
  GY-5150 (MPU-9150): Placa GY-5150 basada en conjunto de acelerómetro+giroscopios+magnetómetro MPU-9150
