# Fritzing sketch arduino and pcf8575 example (saved by Fritzing 0.9.3b)

parts:
  U1 = PCF8575C [package=so-24dw]
  Part1 = Arduino Uno (Rev3)
  R1 = Resistor [tolerance=±5% resistance=220 package=THT]
  LED1 = LED - 5mm [color="Red (633nm)" package="5 mm [THT]"]

nets:
  N1: U1.PO0, R1.Pin_0
  GND: U1.GND, Part1.GND, LED1.cathode
  N2: U1.SCL, Part1.A5/SCL
  N3: U1.SDA, Part1.A4/SDA
  VCC: U1.VCC, Part1.5V
  N4: R1.Pin_1, LED1.anode

notes:
  Schematic only shows 1 led and resistor, the LEDs may be very dim depending on the value of the resistor
