# Fritzing sketch arduino and qyf-TM1638 (saved by Fritzing 0.9.3b)

parts:
  Part1 = Arduino Uno (Rev3)
  J1 = female pin header, 5 pins [form="♀ (female)"]

nets:
  N1: Part1.D8, J1.pin2
  N2: Part1.D9_PWM, J1.pin3
  N3: Part1.D10_PWM/SS, J1.pin4
  N4: Part1.GND, J1.pin1
  N5: Part1.5V, J1.pin5

notes:
  Pinout
  1 - GND
  2 - GND
  3 - STB
  4 - CLK
  5 - VCC
